// Logisim project 1805116.circ as structural Verilog: 1 circuit, main circuit main
module main (
  input  A,
  input  B,
  input  C,
  input  D,
  output O
);

  wire n7404_1_p2, n7404_1_p6, n7404_1_p8, n7404_1_p10, n7408_1_p3, n7408_1_p6, n7408_1_p11, n7408_1_p14,
       n7408_2_p3, n7408_2_p6, n7408_2_p11, n7408_2_p14, n7432_1_p4, n7432_1_p7;

  // _7404 7404_1: pin names not known; wires that end beside it: D, n7404_1_p2, 1'b0, 1'b1, B, n7404_1_p6, C, n7404_1_p8, A, n7404_1_p10
  // _7408 7408_1: pin names not known; wires that end beside it: n7404_1_p2, n7404_1_p6, n7408_1_p3, n7408_1_p3, C, n7408_1_p6, 1'b0, 1'b1, n7404_1_p10, B, n7408_1_p11, n7408_1_p11, n7404_1_p8, n7408_1_p14, A, B, C
  // _7408 7408_2: pin names not known; wires that end beside it: D, n7404_1_p6, n7408_2_p3, n7408_2_p3, n7404_1_p8, n7408_2_p6, 1'b0, 1'b1, n7404_1_p8, n7404_1_p2, n7408_2_p11, n7408_2_p11, B, n7408_2_p14
  // _7432 7432_1: pin names not known; wires that end beside it: D, n7408_2_p6, n7408_1_p14, n7432_1_p4, n7432_1_p4, n7408_1_p6, n7432_1_p7, 1'b0, 1'b1, n7408_2_p14, n7432_1_p7, O

  // Notes on the sheet:
  //   B'C'D+B'CD'+A'BC'+BC'D'
  //   B'CD'
  //   A'BC'
  //   B'C'D
  //   BC'D'
endmodule
