// Logisim project 1805116_ONLINE_2.circ as structural Verilog: 1 circuit, main circuit main
module main (
  input  P,
  input  Q,
  input  R,
  input  S,
  output O
);

  // _7432 7432_1: pin names not known; wires that end beside it: P, R, Q, S, O, 1'b0, 1'b1
endmodule
