// Logisim project 1805116_dld_online3.circ as structural Verilog: 1 circuit, main circuit main
module main (
  input  in_1,
  input  in_2,
  input  B,
  input  C,
  input  D,
  input  A,
  input  in_7,
  input  in_8,
  input  E,
  output O
);

  wire n74157_1_p4;

  // _74157 74157_1: pin names not known; wires that end beside it: D, in_1, in_2, n74157_1_p4, 1'b0, D
  // _74151 74151_1: pin names not known; wires that end beside it: D, n74157_1_p4, n74157_1_p4, E, n74157_1_p4, in_8, O, E, in_7, D, in_7, D, C, B, A
endmodule
