// Logisim project 1805116_DLD_ONLINE_ENCODER.circ as structural Verilog: 1 circuit, main circuit main
module main (
  input  D0,
  input  D1,
  input  D2,
  input  D3,
  output Y1,
  output Y0
);

  wire n7404_1_p3, n7404_1_p5, n7408_1_p3;

  // _7404 7404_1: pin names not known; wires that end beside it: D2, D0, n7404_1_p3, D1, n7404_1_p5
  // _7408 7408_1: pin names not known; wires that end beside it: n7404_1_p3, n7404_1_p5, n7408_1_p3
  // _7432 7432_1: pin names not known; wires that end beside it: D1, D3, Y0, D3, n7408_1_p3, Y1

  // Notes on the sheet:
  //   D0' * D1'
  //   D0'
  //   D1'
  //   D1 + D3
  //   D3 + D0'D1'
endmodule
