// Logisim project 1805116_counter_online.circ as structural Verilog: 1 circuit, main circuit main
module main (
  output Yb,
  output Ya
);

  wire clock_1_out, n7476_1_p5;

  Clock clock_1 (.out(clock_1_out));
  // _7476 7476_1: pin names not known; wires that end beside it: clock_1_out, 1'b1, 1'b1, Ya, n7476_1_p5
  // _7476 7476_2: pin names not known; wires that end beside it: clock_1_out, n7476_1_p5, n7476_1_p5, Yb

  // Notes on the sheet:
  //   Y'a
  //   Yb
endmodule
