// Logisim project 1805116_online6.circ as structural Verilog: 1 circuit, main circuit main
module main (
  output out_1,
  output out_2,
  output out_3
);

  wire clock_1_out, n7408_1_p3, n7408_1_p6, n7408_1_p9, n7476_1_p2, n7476_1_p5, n7476_2_p2, n7476_2_p5;

  Clock clock_1 (.out(clock_1_out));
  // _7476 7476_1: pin names not known; wires that end beside it: clock_1_out, n7476_1_p2, n7476_1_p2, out_3, n7476_1_p5
  // _7476 7476_2: pin names not known; wires that end beside it: clock_1_out, n7476_2_p2, n7476_2_p2, out_2, n7476_2_p5
  // _7408 7408_1: pin names not known; wires that end beside it: out_3, out_2, n7408_1_p3, n7476_1_p5, n7476_2_p5, n7408_1_p6, n7476_1_p5, out_2, n7408_1_p9
  // _7432 7432_1: pin names not known; wires that end beside it: n7408_1_p3, n7408_1_p6, n7476_1_p2, n7408_1_p9, out_1, n7476_2_p2
  // _7476 7476_3: pin names not known; wires that end beside it: clock_1_out, n7476_2_p5, n7476_2_p5, out_1

  // Notes on the sheet:
  //   JK0
  //   JK1
  //   Q1Q0
  //   Q1'Q0'
  //   JK2
endmodule
