// Logisim project 1805116_dld_onlinesequence.circ as structural Verilog: 1 circuit, main circuit main
module main (
  input  x1,
  input  x2
);

  wire clock_1_out, n7404_1_p1, n7404_1_p3, n7408_1_p3, n7408_1_p5, n7432_1_p5;

  Clock clock_1 (.out(clock_1_out));
  // _7404 7404_1: pin names not known; wires that end beside it: n7404_1_p1, x2, n7404_1_p3, x1, n7404_1_p1
  // _7408 7408_1: pin names not known; wires that end beside it: n7404_1_p3, x1, n7408_1_p3, n7404_1_p3, n7408_1_p5
  // _7432 7432_1: pin names not known; wires that end beside it: x1, x2, n7408_1_p3, n7408_1_p5, n7432_1_p5
  // _7476 7476_1: pin names not known; wires that end beside it: clock_1_out, n7432_1_p5, n7432_1_p5
  // _7476 7476_2: pin names not known; wires that end beside it: clock_1_out, n7408_1_p5
endmodule
